# Fritzing sketch Water_Meter (saved by Fritzing 0.9.3b)

parts:
  YF-S201_Flow_Meter1 = YF-S201 Water Flow Meter
  Raspberry_Pi1 = Raspberry Pi 2

nets:
  N1: YF-S201_Flow_Meter1.SIG, Raspberry_Pi1.GPIO4
  GND: YF-S201_Flow_Meter1.GND, Raspberry_Pi1.GND
  VCC: YF-S201_Flow_Meter1.VCC, Raspberry_Pi1.5V

custom parts:
  YF-S201 Water Flow Meter: The YF-S201 Flow Meter. The input voltage is 5V to 24V (DC).
